# Fritzing sketch tow (saved by Fritzing 0.9.3b)
circuit board: 13.8433cm x 4.56046cm
breadboards: 1

parts:
  U1 = atmega328 [package=dip]
  R1 = Resistor [tolerance=±5% resistance=10k package=THT]
  S1 = Pushbutton [package="[SMD]"]
  ISP = AVR ISP 6 Pin [package=2x3_lock]
  XTAL1 = Crystal [frequency="16 Mhz" package=THT]
  C1 = Ceramic Capacitor [capacitance=33pF package="100 mil [THT, multilayer]"]
  C2 = Ceramic Capacitor [capacitance=33pF package="100 mil [THT, multilayer]"]
  S2 = Pushbutton [package="[SMD]"]
  S3 = Pushbutton [package="[SMD]"]
  LED1 = LED - 5mm [color="White (6500K)" package="5 mm [THT]"]
  R2 = Resistor [tolerance=±5% resistance=150 package=THT]
  R3 = Resistor [tolerance=±5% resistance=150 package=THT]
  LED2 = LED - 5mm [color="White (6500K)" package="5 mm [THT]"]
  R4 = Resistor [tolerance=±5% resistance=150 package=THT]
  R5 = Resistor [tolerance=±5% resistance=150 package=THT]
  LED3 = LED - 5mm [color="White (6500K)" package="5 mm [THT]"]
  LED4 = LED - 5mm [color="White (6500K)" package="5 mm [THT]"]
  R6 = Resistor [tolerance=±5% resistance=150 package=THT]
  LED5 = LED - 5mm [color="Red (635nm)" package="5 mm [THT]"]
  R7 = Resistor [tolerance=±5% resistance=150 package=THT]
  R8 = Resistor [tolerance=±5% resistance=150 package=THT]
  R9 = Resistor [tolerance=±5% resistance=150 package=THT]
  R10 = Resistor [tolerance=±5% resistance=150 package=THT]
  LED6 = LED - 5mm [color="White (6500K)" package="5 mm [THT]"]
  LED7 = LED - 5mm [color="White (6500K)" package="5 mm [THT]"]
  LED8 = LED - 5mm [color="White (6500K)" package="5 mm [THT]"]
  LED9 = LED - 5mm [color="White (6500K)" package="5 mm [THT]"]
  U2 = Voltage Regulator - 5V [package="TO220 [THT]"]
  C3 = Ceramic Capacitor [capacitance=0.33µF package="100 mil [THT, multilayer]"]
  C4 = Electrolytic Capacitor [capacitance=1μF package="0405 [SMD, electrolytic]"]
  BAT1 = BC9VPC [package=bc9vpc]
  S4 = Toggle Switch [package=THT]

nets:
  N1: U1.RESET, R1.Pin_0, S1.Pin_1, S1.Pin_2, ISP.5
  N2: U1.D0_(RX), LED1.anode
  N3: U1.D1_(TX), LED2.anode
  N4: U1.D2, LED3.anode
  N5: U1.D3_(PWM), LED4.anode
  N6: U1.D4, LED9.anode
  N7: U1.VCC, U1.D10_(PWM), U1.AVCC, U1.AREF, U1.A1, U1.A2, U1.A3, U1.A4, U1.A5, R1.Pin_1, ISP.2, U2.output_voltage, C4.+
  GND: U1.GND, S1.Pin_3, S1.Pin_4, ISP.6, C1.0, C2.0, S2.Pin_3, S2.Pin_4, S3.Pin_3, S3.Pin_4, R2.Pin_1, R3.Pin_1, R4.Pin_1, R5.Pin_1, R6.Pin_1, R7.Pin_1, R8.Pin_1, R9.Pin_1, R10.Pin_1
  N8: U1.XLAT1, XTAL1.pin_1, C1.1
  N9: U1.XLAT2, XTAL1.pin_0, C2.1
  N10: U1.D5_(PWM), LED8.anode
  N11: U1.D6_(PWM), LED7.anode
  N12: U1.D7, LED6.anode
  N13: U1.D8, S2.Pin_1, S2.Pin_2
  N14: U1.D9_(PWM), S3.Pin_1, S3.Pin_2
  N15: U1.D11_(PWM), ISP.4
  N16: U1.D12, ISP.1
  N17: U1.D13, ISP.3
  N18: U1.A0, LED5.anode
  N19: LED1.cathode, R2.Pin_0
  N20: R3.Pin_0, LED2.cathode
  N21: R4.Pin_0, LED4.cathode
  N22: R5.Pin_0, LED3.cathode
  N23: R6.Pin_0, LED5.cathode
  N24: R7.Pin_0, LED6.cathode
  N25: R8.Pin_0, LED9.cathode
  N26: R9.Pin_0, LED8.cathode
  N27: R10.Pin_0, LED7.cathode
  N28: U2.input_voltage, C3.1, S4.L1
  N29: U2.GND, C3.0, C4.-, BAT1.V-
  N30: BAT1.V+, S4.COM
